# Fritzing sketch Circuito (saved by Fritzing 0.8.7b)
circuit board: 15cm x 15cm
circuit board: 15cm x 15cm
circuit board: 8.46667cm x 5.64444cm
breadboards: 1

parts:
  U2 = Rele Generico [package=relay-g5q]
  R26 = Resistor [tolerance=±5% resistance=1k package=THT]
  U12 = Optocoupler [package=THT]
  Q10 = NPN-Transistor [package="TO92 [THT]"]
  J47 = screw terminal, 3 pins
  J53 = rounded female pin header, 4 pins [form="♀ (female rounded)"]
  Q11 = Basic FET P-Channel [package="TO220 [THT]"]
  Q12 = Basic FET P-Channel [package="TO220 [THT]"]
  Q13 = Basic FET P-Channel [package="TO220 [THT]"]
  R28 = Resistor [tolerance=±5% resistance=1k package=THT]
  U13 = Optocoupler [package=THT]
  Q14 = NPN-Transistor [package="TO92 [THT]"]
  R29 = Resistor [tolerance=±5% resistance=1k package=THT]
  R30 = Resistor [tolerance=±5% resistance=1k package=THT]
  R33 = Resistor [tolerance=±5% resistance=220 package=THT]
  R34 = Resistor [tolerance=±5% resistance=220 package=THT]
  R35 = Resistor [tolerance=±5% resistance=220 package=THT]
  U3 = Rele Generico [package=relay-g5q]
  J45 = screw terminal, 3 pins
  J45_2 = screw terminal, 3 pins
  D1 = Rectifier Diode [part_number=1N4001 package="300 mil [THT]"]
  D2 = Rectifier Diode [part_number=1N4001 package="300 mil [THT]"]
  Q15 = NPN-Transistor [package="TO92 [THT]"]
  S1 = Pushbutton [package="[THT]"]
  U1 = ESP-WROOM-02 WiFi MCU module [part_number=ESP-WROOM-02]
  C1 = Electrolytic Capacitor [capacitance=1µF package="100 mil [THT, electrolytic]"]
  J55 = rounded female alternating pin header, 3 pins [form="♀ (female rounded)"]
  J56 = rounded female pin header, 3 pins [form="♀ (female rounded)"]
  LED1 = LED - 5mm [color="Red (633nm)" package="5 mm [THT]"]
  R36 = Resistor [tolerance=±5% resistance=1k package=THT]
  Pad1 = Pad [width=4 height=2.5 connect=center]
  S2 = Pushbutton [package="[THT]"]

nets:
  N1: U2.BOBINA2, Q10.C, D1.cathode
  N2: U2.ENTRADA, J45.pin2, J45_2.pin2
  N3: U2.NA, J45.pin1, J45_2.pin1
  N4: U2.NF, J45.pin3, J45_2.pin3
  N5: U2.BOBINA1, U12.Pin_5, U13.Pin_5, U3.BOBINA1, D1.anode, D2.anode, Q15.C, S1.Pin_1, S1.Pin_2, U1.10_IO4, C1.+, J56.pin1, R36.Pin_0, S2.Pin_3, S2.Pin_4
  N6: R26.Pin_0, U1.16_TOUT
  N7: R26.Pin_1, U12.Pin_4
  N8: U12.Pin_1, R30.Pin_0
  N9: U12.Pin_2, Q10.E, J53.pin1, U13.Pin_2, Q14.E, Q15.E, LED1.anode
  N10: Q10.B, R30.Pin_1
  N11: J47.pin1, U3.NA
  N12: J47.pin2, U3.ENTRADA
  N13: J47.pin3, U3.NF
  N14: J53.pin2, Q11.drain
  N15: J53.pin3, Q12.drain
  N16: J53.pin4, Q13.drain
  N17: Q11.gate, R33.Pin_1
  N18: Q11.source, Q12.source, Q13.source
  N19: Q12.gate, R34.Pin_1
  N20: Q13.gate, R35.Pin_1
  N21: R28.Pin_0, U13.Pin_4
  N22: R28.Pin_1, U1.12_IO1/TXD
  N23: U13.Pin_1, R29.Pin_0
  N24: Q14.B, R29.Pin_1
  N25: Q14.C, U3.BOBINA2, D2.cathode
  N26: R33.Pin_0, U1.15_RST
  N27: R34.Pin_0, U1.14_IO5
  N28: R35.Pin_0, J56.pin3
  N29: Q15.B, U1.9_GND, U1.13_GND, U1.18_GND, C1.-, J56.pin2, Pad1.pad, S2.Pin_1, S2.Pin_2
  N30: S1.Pin_3, S1.Pin_4, U1.11_IO3/RXD
  N31: U1.6_IO15, J55.pin1
  N32: U1.7_IO2, J55.pin2
  N33: U1.8_IO0, J55.pin3
  N34: LED1.cathode, R36.Pin_1

custom parts:
  Rele Generico: MPA-S-105-C
  ESP-WROOM-02 WiFi MCU module: ESP-WROOM-02 by espressif, Well supported Arduino libraries are available.
